# Fritzing sketch Solar_Thermal_Monitor (saved by Fritzing 0.7.10b)
breadboards: 1

parts:
  Nano1 = Arduino Nano v2.3
  S1 = Pushbutton [package="[THT]"]
  U1 = mystery part, 20 pins [chip_label="FTTL-655S LED Display" part_number=FTTL-655S]
  J1 = male pin header, 2 pins [form="♂ (male)"]
  J2 = male pin header, 2 pins [form="♂ (male)"]
  C1 = Electrolytic Capacitor [capacitance=47µF voltage=16V package="100 mil [THT, electrolytic]"]
  R2 = Resistor [tolerance=±5% resistance=220 package=THT]
  R3 = Resistor [tolerance=±5% resistance=220 package=THT]
  R1 = Resistor [tolerance=±5% resistance=220 package=THT]

nets:
  N1: Nano1.GND, S1.Pin_1, S1.Pin_2, J1.pin1, J2.pin1, C1.-, R3.Pin_0
  N2: Nano1.D2, U1.pin20
  N3: Nano1.D3, U1.pin19
  N4: Nano1.D4, U1.pin18
  N5: Nano1.D5, U1.pin17
  N6: Nano1.D6, U1.pin16
  N7: Nano1.D7, U1.pin15
  N8: Nano1.D8, U1.pin14
  N9: Nano1.D9, U1.pin2
  N10: Nano1.D10, U1.pin1
  N11: Nano1.D12, S1.Pin_4
  N12: Nano1.D13, J1.pin2, R1.Pin_1
  N13: Nano1.A0, R2.Pin_1, R3.Pin_1
  N14: Nano1.+5V, R1.Pin_0
  N15: J2.pin2, C1.+, R2.Pin_0
