# Fritzing sketch Solar_Thermal_Monitor (saved by Fritzing 0.6.3b)
breadboards: 1

parts:
  Nano1 = Arduino Nano v2.3
  S1 = Pushbutton [package="[THT]"]
  J1 = female pin header, 2 pins [form="♂ (male)"]
  J2 = female pin header, 2 pins [form="♂ (male)"]
  C1 = Electrolytic Capacitor [capacitance=47µF voltage=16V package="100 mil [THT, electrolytic]"]
  R2 = Resistor [tolerance=±5% resistance=220 package=THT]
  R3 = Resistor [tolerance=±5% resistance=220 package=THT]
  R1 = Resistor [tolerance=±5% resistance=220 package=THT]
  U1 = mystery part, 20 pins [chip_label=? spacing=300mil]  # not connected

nets:
  N1: Nano1.GND, S1.Pin_1, S1.Pin_2, J1.pin1, J2.pin1, C1.-, R3.Pin_0
  N2: Nano1.D12, S1.Pin_4
  N3: Nano1.D13, J1.pin2, R1.Pin_1
  N4: Nano1.A0, R2.Pin_1, R3.Pin_1
  N5: Nano1.+5V, R1.Pin_0
  N6: J2.pin2, C1.+, R2.Pin_0
